# Fritzing sketch Esquema CNC (saved by Fritzing 1.0.2b)
breadboards: 1

parts:
  Componente1 = Arduino Mega 2560 (Rev3)
  M2 = Stepper Motor - Bipolar
  M3 = Stepper Motor - Bipolar
  J2 = Basic Servo
  J3 = Basic Servo
  Arduino_CNC_Shield_V3_00_1 = Arduino_CNC_V3.00
  M4 = Stepper Motor - Bipolar
  J4 = Basic Servo
  VCC1 = Battery block 9V
  BAT1 = Battery Holders [package=lipo-1100mAh]

nets:
  N1: Componente1.D48, J4.pulse
  N2: Componente1.D49, J2.pulse
  N3: Componente1.D50, J3.pulse
  GND: Componente1.GND, J2.gnd, J3.gnd, J4.gnd, BAT1.-
  N4: M2.A, Arduino_CNC_Shield_V3_00_1.X-MTR_'3'
  N5: M2.C, Arduino_CNC_Shield_V3_00_1.X-MTR_'4'
  N6: M2.B, Arduino_CNC_Shield_V3_00_1.X-MTR_'2'
  N7: M2.D, Arduino_CNC_Shield_V3_00_1.X-MTR_'1'
  N8: M3.A, Arduino_CNC_Shield_V3_00_1.Z-MTR_'1'
  N9: M3.C, Arduino_CNC_Shield_V3_00_1.Z-MTR_'2'
  N10: M3.B, Arduino_CNC_Shield_V3_00_1.Z-MTR_'4'
  N11: M3.D, Arduino_CNC_Shield_V3_00_1.Z-MTR_'3'
  VCC: J2.vcc, J3.vcc, J4.vcc, BAT1.+
  N12: Arduino_CNC_Shield_V3_00_1.POWER_-, VCC1.-
  N13: Arduino_CNC_Shield_V3_00_1.POWER_+, VCC1.+
  N14: Arduino_CNC_Shield_V3_00_1.Y-MTR_'1', M4.B
  N15: Arduino_CNC_Shield_V3_00_1.Y-MTR_'2', M4.D
  N16: Arduino_CNC_Shield_V3_00_1.Y-MTR_'3', M4.C
  N17: Arduino_CNC_Shield_V3_00_1.Y-MTR_'4', M4.A

custom parts:
  Arduino_CNC_V3.00: Protoneer Arduino CNC Shield V3.00 If using Grbl V0.9: The “A” axis can not be used (yet). The “SCL” (Arduino A5) pin is now used for 'Probing' input. The “End Stops Z+ & Z-” (Arduino D11) and “SpnEn” (Arduino D12) have been switched!
